// Logisim project ULA.circ as structural Verilog
module meiosomador (
  input  in_1,
  input  in_2,
  output out_3,
  output out_4
);

  xor Soma (out_3, in_1, in_2);
  and Carry_In (out_4, in_1, in_2);
endmodule

module somadorcompleto (
  input  Cin,
  input  A,
  input  B,
  output \Saída_Soma ,
  output Cout
);

  wire A___B_out, A___Cin_out, B__Cin_out, Soma_out;

  xor Soma (Soma_out, A, B);
  and A___B (A___B_out, A, B);
  and A___Cin (A___Cin_out, A, Cin);
  and B__Cin (B__Cin_out, B, Cin);
  xor plus_Cin (\Saída_Soma , Cin, Soma_out);
  or Out (Cout, A___B_out, A___Cin_out, B__Cin_out);
endmodule

module MUX32 (
  input  E0,
  input  E1,
  input  E2,
  input  E3,
  input  E4,
  input  E5,
  input  E6,
  input  E7,
  input  E8,
  input  E9,
  input  E10,
  input  E11,
  input  E12,
  input  E13,
  input  E14,
  input  E15,
  input  E16,
  input  E17,
  input  E18,
  input  E19,
  input  E20,
  input  E21,
  input  E22,
  input  E23,
  input  E24,
  input  E25,
  input  E26,
  input  E27,
  input  E28,
  input  E29,
  input  E30,
  input  E31
);
endmodule

module MUX4 (
  input  in_1,
  input  in_2,
  input  in_3,
  input  in_4,
  input  in_5,
  input  in_6
);

  // AND_Gate and_1 has open pins: in0=in_1, in1=in_5, in2=in_6, out=open
  // AND_Gate and_2 has open pins: in0=in_2, in1=in_5, in2=in_6, out=open
  // AND_Gate and_3 has open pins: in0=in_3, out=open
  // AND_Gate and_4 has open pins: in0=in_4, out=open
endmodule

module MUX16 (
  input  in_1,
  input  in_2,
  input  in_3,
  input  in_4,
  input  in_5,
  input  in_6,
  input  in_7,
  input  in_8,
  input  in_9,
  input  in_10,
  input  in_11,
  input  in_12,
  input  in_13,
  input  in_14,
  input  in_15,
  input  in_16,
  input  in_17,
  input  in_18,
  input  in_19,
  input  in_20
);

  wire mux4_1_p5, mux4_2_p5, mux4_3_p5, mux4_4_p5;

  // MUX4 mux4_1: pin names not known; wires that end beside it: in_1, in_2, in_3, in_4, mux4_1_p5
  // MUX4 mux4_2: pin names not known; wires that end beside it: in_5, in_6, in_7, in_8, mux4_2_p5
  // MUX4 mux4_3: pin names not known; wires that end beside it: in_9, in_10, in_11, in_12, mux4_3_p5
  // MUX4 mux4_4: pin names not known; wires that end beside it: in_13, in_14, in_15, in_16, mux4_4_p5
  // MUX4 mux4_5: pin names not known; wires that end beside it: mux4_1_p5, mux4_2_p5, mux4_3_p5, mux4_4_p5
endmodule
